# Fritzing sketch PCBv3_phylab (saved by Fritzing 0.9.0b)
circuit board: 5cm x 5cm
breadboards: 1

parts:
  NRF24L01+ = double row female pin header, 8 pins [form="♀ (female)"]
  C1 = Electrolytic Capacitor [capacitance=1µF package="100 mil [THT, electrolytic]"]
  Part1 = Arduino Micro (Rev3)
  U2 = Voltage Regulator - 5V [package="TO220 [THT]"]
  SENSOR = female pin header, 6 pins [form="♀ (female)"]
  D1 = Rectifier Diode [part_number=1N4001 package="300 mil [THT]"]
  U4 = Voltage Regulator [package=sot223]
  U5 = atmega168 [package=dip]
  R1 = Resistor [tolerance=±5% resistance=220 package=THT]
  ISP = double row female pin header, 6 pins [form="♀ (female)"]
  7-20V_DC_IN = Power plug
  C3 = Electrolytic Capacitor [capacitance=1µF package="100 mil [THT, electrolytic]"]
  C2 = Electrolytic Capacitor [capacitance=10µF package="100 mil [THT, electrolytic]"]
  5v_3_3v_GND = female pin header, 4 pins [form="♀ (female)"]

nets:
  GND: NRF24L01+.pin1, Part1.GND, U2.GND, U4.ADJ, U5.GND, ISP.pin1, 7-20V_DC_IN.GND, C3.-, 5v_3_3v_GND.pin4
  N1: NRF24L01+.pin2, Part1.D5_PWM, U5.A0
  N2: NRF24L01+.pin3, Part1.SCK, U5.D13, ISP.pin5
  N3: NRF24L01+.pin4, Part1.MISO, U5.D12, ISP.pin4
  N4: NRF24L01+.pin5, Part1.D3/SCL
  N5: NRF24L01+.pin6, Part1.MOSI, U5.D11_(PWM), ISP.pin2
  N6: NRF24L01+.pin7, Part1.D6_PWM/A7, U5.A1
  N7: NRF24L01+.pin8, C1.+, U4.OUT, 5v_3_3v_GND.pin2
  N8: C1.-, C2.-
  N9: Part1.RESET, U5.RESET, R1.Pin_0, ISP.pin6
  5V: Part1.5V, U2.output_voltage, U4.IN, U5.VCC, U5.AVCC, R1.Pin_1, ISP.pin3, C2.+, 5v_3_3v_GND.pin1
  N10: Part1.A5, SENSOR.pin6, U5.D4
  N11: Part1.A4, SENSOR.pin5, U5.D3_(PWM)
  N12: Part1.A3, SENSOR.pin4, U5.D2, U5.A2
  N13: Part1.A2, SENSOR.pin3, U5.D1_(TX), U5.A3
  N14: Part1.A1, SENSOR.pin2, U5.D0_(RX), U5.A4
  N15: Part1.A0, SENSOR.pin1, U5.A5
  N16: U2.input_voltage, D1.cathode, C3.+, 5v_3_3v_GND.pin3
  N17: D1.anode, 7-20V_DC_IN.VCC

notes:
  J1
  J2
  J3
  J4
  5V 3.3V VIN GND
  PhyLab
  https://lizzit.it/phylab
  rev1
