# Fritzing sketch raspi_phylab_v1 (saved by Fritzing 0.9.0b)
circuit board: 2.22873cm x 3.43947cm
breadboards: 1

parts:
  J1 = Generic double row female header - 8 pins [form="♀ (female)" package=THT]
  J2 = double row female pin header, 24 pins [form="♀ (female)"]
  C1 = Tantalum Capacitor [capacitance=0.1µF package="D 7343 [SMD, tantalum]"]
  C2 = Tantalum Capacitor [capacitance=0.1µF package="D 7343 [SMD, tantalum]"]
  C3 = Tantalum Capacitor [capacitance=0.1µF package="D 7343 [SMD, tantalum]"]
  C4 = Tantalum Capacitor [capacitance=0.1µF package="D 7343 [SMD, tantalum]"]

nets:
  N1: J1.gnd, J2.pin5, C1.-, C2.-, C3.-, C4.-
  N2: J1.ce, J2.pin14
  N3: J1.sck, J2.pin12
  N4: J1.miso, J2.pin11
  N5: J1.mosi, J2.pin10
  N6: J1.csn, J2.pin16
  N7: J1.vcc, J2.pin1, C1.+, C2.+, C3.+, C4.+

notes:
  nRF24L01+
  PhyLab
  https://lizzit.it/phylab
  rev1

custom parts:
  Generic double row female header - 8 pins: Generic double row female header
